// Logisim project final_circuit.circ as structural Verilog
module main (
);

  wire [9:0] button_7_out;

  Button button_1 (.out(button_7_out[2]));
  Button button_2 (.out(button_7_out[1]));
  Button button_3 (.out(button_7_out[5]));
  Button button_4 (.out(button_7_out[4]));
  Button button_5 (.out(button_7_out[7]));
  Button button_6 (.out(button_7_out[8]));
  Button button_7 (.out(button_7_out[0]));
  Button button_8 (.out(button_7_out[3]));
  Button button_9 (.out(button_7_out[6]));
  Button button_10 (.out(button_7_out[9]));
  RAM_16x8 ram_16x8_1 ();  // open: Data_in, Mode, Data_out, CLK, Address
  Button_Handler button_handler_1 (.I(button_7_out));  // open: O, CS
  _7_Segment_Display u_7_segment_display_1 ();  // open: g, f, a, b, e, d, c, dp
  _7_Segment_Display u_7_segment_display_2 ();  // open: g, f, a, b, e, d, c, dp
  _7_Segment_Display u_7_segment_display_3 ();  // open: g, f, a, b, e, d, c, dp
endmodule

module Button_Handler (
  input  [9:0] I,
  input  CS,
  output [7:0] O
);

  wire controlled_buffer_1_out, not_1_out, or_5_out;
  wire [3:0] byte_reg_1_o, or_3_out;
  wire [7:4] byte_reg_1_o_2;

  or or_1 (or_3_out[3], I[9], I[8]);
  or or_2 (or_3_out[2], I[7], I[6], I[5], I[4]);
  or or_3 (or_3_out[0], I[9], I[7], I[5], I[3], I[1]);
  or or_4 (or_3_out[1], I[7], I[6], I[3], I[2]);
  or or_5 (or_5_out, I[0], or_3_out[3], or_3_out[2], or_3_out[1], or_3_out[0]);
  assign controlled_buffer_1_out = not_1_out ? or_5_out : 1'bz;  // Controlled_Buffer controlled_buffer_1
  not not_1 (not_1_out, CS);
  Byte_Reg byte_reg_1 (
    .Chip_Select(1'b1), .Clock(controlled_buffer_1_out), .Mode_RW(controlled_buffer_1_out),
    .O({byte_reg_1_o_2, byte_reg_1_o}), .I({byte_reg_1_o, or_3_out}));
  assign O = CS ? {byte_reg_1_o_2, byte_reg_1_o} : 8'bz;  // Controlled_Buffer controlled_buffer_2
endmodule

module RAM_16x8 (
  input  CLK,
  input  Mode,
  input  [3:0] Address,
  input  [7:0] Data_in,
  output [7:0] Data_out
);

  wire d_ff_1_q, decoder_1_out0, decoder_1_out1, decoder_1_out2, decoder_1_out3, decoder_1_out4,
       decoder_1_out5, decoder_1_out6, decoder_1_out7, decoder_1_out8, decoder_1_out9, decoder_1_out10,
       decoder_1_out11, decoder_1_out12, decoder_1_out13, decoder_1_out14, decoder_1_out15, t_ff_1_q;
  wire [3:0] d_ff_5_q;

  Byte_Reg R_0 (.Chip_Select(decoder_1_out0), .Clock(CLK), .Mode_RW(d_ff_1_q), .O(Data_in), .I(Data_out));
  Byte_Reg R_4 (.Chip_Select(decoder_1_out4), .Clock(CLK), .Mode_RW(d_ff_1_q), .O(Data_in), .I(Data_out));
  Byte_Reg R_8 (.Chip_Select(decoder_1_out8), .Clock(CLK), .Mode_RW(d_ff_1_q), .O(Data_in), .I(Data_out));
  Byte_Reg R_12 (.Chip_Select(decoder_1_out12), .Clock(CLK), .Mode_RW(d_ff_1_q), .O(Data_in), .I(Data_out));
  Byte_Reg R_1 (.Chip_Select(decoder_1_out1), .Clock(CLK), .Mode_RW(d_ff_1_q), .O(Data_in), .I(Data_out));
  Byte_Reg R_5 (.Chip_Select(decoder_1_out5), .Clock(CLK), .Mode_RW(d_ff_1_q), .O(Data_in), .I(Data_out));
  Byte_Reg R_9 (.Chip_Select(decoder_1_out9), .Clock(CLK), .Mode_RW(d_ff_1_q), .O(Data_in), .I(Data_out));
  Byte_Reg R_13 (.Chip_Select(decoder_1_out13), .Clock(CLK), .Mode_RW(d_ff_1_q), .O(Data_in), .I(Data_out));
  Byte_Reg D (.Chip_Select(1'b1), .Clock(CLK), .Mode_RW(t_ff_1_q), .O(Data_out), .I(Data_in));
  Byte_Reg R_2 (.Chip_Select(decoder_1_out2), .Clock(CLK), .Mode_RW(d_ff_1_q), .O(Data_in), .I(Data_out));
  Byte_Reg R_6 (.Chip_Select(decoder_1_out6), .Clock(CLK), .Mode_RW(d_ff_1_q), .O(Data_in), .I(Data_out));
  Byte_Reg R_10 (.Chip_Select(decoder_1_out10), .Clock(CLK), .Mode_RW(d_ff_1_q), .O(Data_in), .I(Data_out));
  Byte_Reg R_14 (.Chip_Select(decoder_1_out14), .Clock(CLK), .Mode_RW(d_ff_1_q), .O(Data_in), .I(Data_out));
  T_Flip_Flop t_ff_1 (.T(1'b1), .clk(CLK), .Q(t_ff_1_q));  // open: Qn, reset, preset
  Byte_Reg R_3 (.Chip_Select(decoder_1_out3), .Clock(CLK), .Mode_RW(d_ff_1_q), .O(Data_in), .I(Data_out));
  Byte_Reg R_7 (.Chip_Select(decoder_1_out7), .Clock(CLK), .Mode_RW(d_ff_1_q), .O(Data_in), .I(Data_out));
  Byte_Reg R_11 (.Chip_Select(decoder_1_out11), .Clock(CLK), .Mode_RW(d_ff_1_q), .O(Data_in), .I(Data_out));
  Byte_Reg R_15 (.Chip_Select(decoder_1_out15), .Clock(CLK), .Mode_RW(d_ff_1_q), .O(Data_in), .I(Data_out));
  Decoder #(.select(4)) decoder_1 (
    .out0(decoder_1_out0), .out1(decoder_1_out1), .out2(decoder_1_out2), .out3(decoder_1_out3),
    .out4(decoder_1_out4), .out5(decoder_1_out5), .out6(decoder_1_out6), .out7(decoder_1_out7),
    .out8(decoder_1_out8), .out9(decoder_1_out9), .out10(decoder_1_out10), .out11(decoder_1_out11),
    .out12(decoder_1_out12), .out13(decoder_1_out13), .out14(decoder_1_out14), .out15(decoder_1_out15),
    .sel(d_ff_5_q), .en(CLK));
  D_Flip_Flop d_ff_1 (.D(Mode), .clk(CLK), .Q(d_ff_1_q));  // open: Qn, preset, reset
  D_Flip_Flop d_ff_2 (.D(Address[3]), .clk(CLK), .Q(d_ff_5_q[3]));  // open: Qn, preset, reset
  D_Flip_Flop d_ff_3 (.D(Address[2]), .clk(CLK), .Q(d_ff_5_q[2]));  // open: Qn, preset, reset
  D_Flip_Flop d_ff_4 (.D(Address[1]), .clk(CLK), .Q(d_ff_5_q[1]));  // open: Qn, preset, reset
  D_Flip_Flop d_ff_5 (.D(Address[0]), .clk(CLK), .Q(d_ff_5_q[0]));  // open: Qn, preset, reset
endmodule

module Stalwart_CPU (
);

  Byte_Reg MAR ();  // open: Chip_Select, Clock, Mode_RW, O, I
  Byte_Reg MBR ();  // open: Chip_Select, Clock, Mode_RW, O, I
  Byte_Reg D0 ();  // open: Chip_Select, Clock, Mode_RW, O, I
  Byte_Reg D1 ();  // open: Chip_Select, Clock, Mode_RW, O, I
  ALU alu_1 ();  // open: A, Status, R, L, OPcode
endmodule

module ALU (
  input  OPcode,
  input  L,
  input  R,
  output Status,
  output A
);
endmodule

module Byte_Reg (
  input  [7:0] I,
  input  Clock,
  input  Mode_RW,
  input  Chip_Select,
  output [7:0] O
);

  wire and_1_out, and_2_out, not_1_out, not_2_out;
  wire [7:0] controlled_buffer_1_out, R_0_q;

  not not_1 (not_1_out, Clock);
  assign controlled_buffer_1_out = and_1_out ? I : 8'bz;  // Controlled_Buffer controlled_buffer_1
  not not_2 (not_2_out, not_1_out);
  and and_1 (and_1_out, Mode_RW, Chip_Select);
  and and_2 (and_2_out, Chip_Select, ~Mode_RW);  // AND_Gate
  D_Flip_Flop R_4 (.D(controlled_buffer_1_out[4]), .clk(not_2_out), .Q(R_0_q[4]));  // open: Qn, preset, reset
  D_Flip_Flop R_5 (.D(controlled_buffer_1_out[5]), .clk(not_2_out), .Q(R_0_q[5]));  // open: Qn, preset, reset
  D_Flip_Flop R_6 (.D(controlled_buffer_1_out[6]), .clk(not_2_out), .Q(R_0_q[6]));  // open: Qn, preset, reset
  D_Flip_Flop R_7 (.D(controlled_buffer_1_out[7]), .clk(not_2_out), .Q(R_0_q[7]));  // open: Qn, preset, reset
  assign O = and_2_out ? R_0_q : 8'bz;  // Controlled_Buffer controlled_buffer_2
  D_Flip_Flop R_0 (.D(controlled_buffer_1_out[0]), .clk(not_2_out), .Q(R_0_q[0]));  // open: Qn, preset, reset
  D_Flip_Flop R_1 (.D(controlled_buffer_1_out[1]), .clk(not_2_out), .Q(R_0_q[1]));  // open: Qn, preset, reset
  D_Flip_Flop R_2 (.D(controlled_buffer_1_out[2]), .clk(not_2_out), .Q(R_0_q[2]));  // open: Qn, preset, reset
  D_Flip_Flop R_3 (.D(controlled_buffer_1_out[3]), .clk(not_2_out), .Q(R_0_q[3]));  // open: Qn, preset, reset
endmodule
